# Fritzing sketch knock_board (saved by Fritzing 0.9.10b)
breadboards: 1

parts:
  IC1 = IC, DIP package, 14 pins [chip_label=IC]
  J3 = male pin header, 5 pins [form="♂ (male)"]
  J4 = male pin header, 2 pins [form="♂ (male)"]
  J5 = male pin header, 2 pins [form="♂ (male)"]
  IC2 = IC, DIP package, 8 pins [chip_label=IC]
  J6 = male pin header, 4 pins [form="♂ (male)"]
  J7 = male pin header, 2 pins [form="♂ (male)"]
  J8 = male pin header, 2 pins [form="♂ (male)"]
  J2 = Dagu DGServo 9g header (male) [package=THT]
  C1 = Electrolytic Capacitor [capacitance=1µF voltage=35V package="200 mil [THT, electrolytic]"]
  C2 = Electrolytic Capacitor [capacitance=1µF voltage=35V package="100 mil [THT, electrolytic]"]
  C3 = Electrolytic Capacitor [capacitance=1µF voltage=35V package="200 mil [THT, electrolytic]"]
  J9 = male pin header, 2 pins [form="♂ (male)"]

nets:
  N1: IC1.pin1, J3.pin4, J5.pin1, J6.pin1, J2.Vcc, C1.+, C3.+
  N2: IC1.pin5, J3.pin3, J9.pin1
  N3: IC1.pin6, J2.gnd
  N4: IC1.pin7, J3.pin2
  N5: IC1.pin9, J3.pin1
  N6: IC1.pin14, J3.pin5, J4.pin2, IC2.pin4, J6.pin4, J7.pin2, J8.pin2, J2.pulse, C1.-, C3.-, J9.pin2
  N7: J4.pin1, IC2.pin5
  N8: J5.pin2, IC2.pin8
  N9: IC2.pin2, J6.pin3
  N10: IC2.pin3, J6.pin2
  N11: IC2.pin6, C2.+
  N12: IC2.pin7, J7.pin1
  N13: J8.pin1, C2.-
